// Logisim project hw3.circ as structural Verilog: 14 circuits, main circuit 1-Bit Adder
module _1_Bit_Adder (
  input  a,
  input  b,
  input  carry_in,
  output sum,
  output carry_out
);

  wire and_2_out, and_3_out, and_4_out, and_5_out, and_6_out, and_7_out, and_8_out, not_1_out, not_2_out,
       not_3_out, not_4_out, not_5_out, not_6_out, not_7_out, not_8_out, not_9_out, not_10_out, not_11_out,
       not_12_out;

  not not_1 (not_1_out, a);
  not not_2 (not_2_out, b);
  not not_3 (not_3_out, carry_in);
  not not_4 (not_4_out, a);
  not not_5 (not_5_out, b);
  not not_6 (not_6_out, a);
  not not_7 (not_7_out, carry_in);
  not not_8 (not_8_out, a);
  not not_9 (not_9_out, b);
  not not_10 (not_10_out, carry_in);
  not not_11 (not_11_out, b);
  not not_12 (not_12_out, carry_in);
  // AND_Gate and_1 has open pins: in0=not_1_out, in1=not_2_out, in2=not_3_out, out=open
  and and_2 (and_2_out, not_4_out, not_5_out, carry_in);
  and and_3 (and_3_out, not_6_out, b, not_7_out);
  and and_4 (and_4_out, not_8_out, b, carry_in);
  and and_5 (and_5_out, a, not_9_out, not_10_out);
  and and_6 (and_6_out, a, not_11_out, carry_in);
  and and_7 (and_7_out, a, b, not_12_out);
  and and_8 (and_8_out, a, b, carry_in);
  or or_1 (sum, and_2_out, and_3_out, and_5_out, and_8_out);
  or or_2 (carry_out, and_4_out, and_6_out, and_7_out, and_8_out);

  // Notes on the sheet:
  //   Note: Do NOT move any of the pins already in this circuit. Moving the pins may cause the checkers to fail.
  //   Yamin Mousselli 
endmodule

module _4_Bit_Adder (
  input  [3:0] a,
  input  [3:0] b,
  input  carry_in,
  output [3:0] sum,
  output carry_out
);

  wire n1_bit_adder_1_carry_out, n1_bit_adder_2_carry_out, n1_bit_adder_3_carry_out;

  _1_Bit_Adder u_1_bit_adder_1 (
    .a(a[0]), .b(b[0]), .carry_in(carry_in), .sum(sum[0]), .carry_out(n1_bit_adder_1_carry_out));
  _1_Bit_Adder u_1_bit_adder_2 (
    .a(a[1]), .b(b[1]), .carry_in(n1_bit_adder_1_carry_out), .sum(sum[1]),
    .carry_out(n1_bit_adder_2_carry_out));
  _1_Bit_Adder u_1_bit_adder_3 (
    .a(a[2]), .b(b[2]), .carry_in(n1_bit_adder_2_carry_out), .sum(sum[2]),
    .carry_out(n1_bit_adder_3_carry_out));
  _1_Bit_Adder u_1_bit_adder_4 (
    .a(a[3]), .b(b[3]), .carry_in(n1_bit_adder_3_carry_out), .sum(sum[3]), .carry_out(carry_out));

  // Notes on the sheet:
  //   Note: Do NOT move any of the pins already in this circuit. Moving the pins may cause the checkers to fail.
endmodule

module _4_Bit_ALU (
  input  [3:0] a,
  input  [3:0] b,
  input  [2:0] operation,
  output [3:0] \output 
);

  wire [3:0] and_1_out, n4_bit_2_scomplementnegation_1_output, n4_bit_adder_1_sum, n4_bit_adder_2_sum,
       n4_bit_multiplyby5_1_output, n4_bitismultipleof4_1_output, not_1_out, not_2_out, or_1_out, xor_1_out;

  assign not_1_out = ~b;  // NOT_Gate not_1, 4 bits wide
  _4_bitIsMultipleOf4 u_4_bitismultipleof4_1 (.in_1(a), .\output (n4_bitismultipleof4_1_output));
  _4_bit_2_sComplementNegation u_4_bit_2_scomplementnegation_1 (
    .in_1(a), .\output (n4_bit_2_scomplementnegation_1_output));
  _4_bit_MultiplyBy5 u_4_bit_multiplyby5_1 (.in_1(a), .\output (n4_bit_multiplyby5_1_output));
  _4_Bit_Adder u_4_bit_adder_1 (.a(a), .b(b), .carry_in(1'b0), .sum(n4_bit_adder_1_sum));  // open: carry_out
  _4_Bit_Adder u_4_bit_adder_2 (.a(a), .b(not_1_out), .carry_in(1'b1), .sum(n4_bit_adder_2_sum));  // open: carry_out
  assign and_1_out = a & b;  // AND_Gate and_1, 4 bits wide
  assign xor_1_out = a ^ b;  // XOR_Gate xor_1, 4 bits wide
  assign or_1_out = a | b;  // OR_Gate or_1, 4 bits wide
  assign not_2_out = ~or_1_out;  // NOT_Gate not_2, 4 bits wide
  Multiplexer #(.select(3), .width(4), .disabled(0), .enable("false")) multiplexer_1 (
    .in0(n4_bit_adder_1_sum), .in1(n4_bit_adder_2_sum), .in2(n4_bitismultipleof4_1_output),
    .in3(n4_bit_2_scomplementnegation_1_output), .in4(n4_bit_multiplyby5_1_output), .in5(and_1_out),
    .in6(xor_1_out), .in7(not_2_out), .out(\output ), .sel(operation));

  // Notes on the sheet:
  //   Subtractor
  //   Multiple of 4
  //   Add
  //   2's Comp.
  //   * by 5
  //   Note: Do NOT move any of the pins already in this circuit. Moving the pins may cause the checkers to fail.
  //   Subtractor: A - B = A + (~B). We add 1 by letting the carry in be represented as 1, due to the fact that it is 2's complement.
endmodule

module _16_Bit_Adder (
  input  [15:0] a,
  input  [15:0] b,
  input  carry_in,
  output [15:0] sum,
  output carry_out
);

  wire n4_bit_adder_1_carry_out, n4_bit_adder_2_carry_out, n4_bit_adder_3_carry_out;

  _4_Bit_Adder u_4_bit_adder_1 (
    .a(a[3:0]), .b(b[3:0]), .carry_in(carry_in), .sum(sum[3:0]), .carry_out(n4_bit_adder_1_carry_out));
  _4_Bit_Adder u_4_bit_adder_2 (
    .a(a[7:4]), .b(b[7:4]), .carry_in(n4_bit_adder_1_carry_out), .sum(sum[7:4]),
    .carry_out(n4_bit_adder_2_carry_out));
  _4_Bit_Adder u_4_bit_adder_3 (
    .a(a[11:8]), .b(b[11:8]), .carry_in(n4_bit_adder_2_carry_out), .sum(sum[11:8]),
    .carry_out(n4_bit_adder_3_carry_out));
  _4_Bit_Adder u_4_bit_adder_4 (
    .a(a[15:12]), .b(b[15:12]), .carry_in(n4_bit_adder_3_carry_out), .sum(sum[15:12]), .carry_out(carry_out));

  // Notes on the sheet:
  //   Note: Do NOT move any of the pins already in this circuit. Moving the pins may cause the checkers to fail.
endmodule

module _16_Bit_ALU (
  input  [15:0] a,
  input  [15:0] b,
  input  [2:0] operation,
  output [15:0] \output 
);

  wire [15:0] and_1_out, n16_bit_2_scomplementnegation_1_output, n16_bit_a_8_1_1_output, n16_bit_adder_1_sum,
       n16_bit_multiplyby11_1_out_2, n16_bit_subtraction_1_out_3, not_1_out, or_1_out, xor_1_out;

  assign and_1_out = a & b;  // AND_Gate and_1, 16 bits wide
  assign xor_1_out = a ^ b;  // XOR_Gate xor_1, 16 bits wide
  _16_Bit_Adder u_16_bit_adder_1 (.a(a), .b(b), .carry_in(1'b0), .sum(n16_bit_adder_1_sum));  // open: carry_out
  _16_Bit_Subtraction u_16_bit_subtraction_1 (.in_1(a), .in_2(b), .out_3(n16_bit_subtraction_1_out_3));
  _16_Bit_2_sComplementNegation u_16_bit_2_scomplementnegation_1 (
    .in_1(a), .\output (n16_bit_2_scomplementnegation_1_output));
  _16_bit_A_8____1 u_16_bit_a_8_1_1 (.in_1(a), .\output (n16_bit_a_8_1_1_output));
  assign or_1_out = a | b;  // OR_Gate or_1, 16 bits wide
  assign not_1_out = ~or_1_out;  // NOT_Gate not_1, 16 bits wide
  _16_bit_MultiplyBy11 u_16_bit_multiplyby11_1 (.in_1(a), .out_2(n16_bit_multiplyby11_1_out_2));
  Multiplexer #(.select(3), .width(16), .disabled(0), .enable("false")) multiplexer_1 (
    .in0(n16_bit_adder_1_sum), .in1(n16_bit_subtraction_1_out_3), .in2(n16_bit_a_8_1_1_output),
    .in3(n16_bit_2_scomplementnegation_1_output), .in4(n16_bit_multiplyby11_1_out_2), .in5(and_1_out),
    .in6(xor_1_out), .in7(not_1_out), .out(\output ), .sel(operation));

  // Notes on the sheet:
  //   Add
  //   2's Comp.
  //   Note: Do NOT move any of the pins already in this circuit. Moving the pins may cause the checkers to fail.
  //   Subtraction
  //   A % 8 == 1
  //   * by 11
endmodule

module Adder_Checkers (
);

  wire n1_bit_adder_checker_1_p1, n1_bit_adder_checker_1_p2, n1_bit_adder_checker_1_p3,
       n1_bit_adder_checker_1_p4, n1_bit_adder_checker_1_p5, n1_bit_adder_checker_1_p6,
       n1_bit_adder_checker_1_p7, n4_bit_adder_checker_1_p3, n4_bit_adder_checker_1_p4,
       n4_bit_adder_checker_1_p5, n4_bit_adder_checker_1_p6, n16_bit_adder_checker_1_p3,
       n16_bit_adder_checker_1_p4, n16_bit_adder_checker_1_p5, n16_bit_adder_checker_1_p6;
  wire [3:0] n4_bit_adder_checker_1_p1, n4_bit_adder_checker_1_p2, n4_bit_adder_checker_1_p7;
  wire [15:0] n16_bit_adder_checker_1_p1, n16_bit_adder_checker_1_p2, n16_bit_adder_checker_1_p7;

  // _1_Bit_Adder_Checker 1_bit_adder_checker_1: pin names not known; wires that end beside it: n1_bit_adder_checker_1_p1, n1_bit_adder_checker_1_p2, n1_bit_adder_checker_1_p3, n1_bit_adder_checker_1_p4, n1_bit_adder_checker_1_p5, n1_bit_adder_checker_1_p6, n1_bit_adder_checker_1_p7
  Clock Clock (.out(n1_bit_adder_checker_1_p4));
  // _16_Bit_Adder_Checker 16_bit_adder_checker_1: pin names not known; wires that end beside it: n16_bit_adder_checker_1_p1, n16_bit_adder_checker_1_p2, n16_bit_adder_checker_1_p3, n16_bit_adder_checker_1_p4, n16_bit_adder_checker_1_p5, n16_bit_adder_checker_1_p6, n16_bit_adder_checker_1_p7
  _1_Bit_Adder u_1_bit_adder_1 (
    .a(n1_bit_adder_checker_1_p1), .b(n1_bit_adder_checker_1_p2), .carry_in(n1_bit_adder_checker_1_p3),
    .sum(n1_bit_adder_checker_1_p7), .carry_out(n1_bit_adder_checker_1_p6));
  Button Reset (.out(n1_bit_adder_checker_1_p5));
  _16_Bit_Adder u_16_bit_adder_1 (
    .a(n16_bit_adder_checker_1_p1), .b(n16_bit_adder_checker_1_p2), .carry_in(n16_bit_adder_checker_1_p3),
    .sum(n16_bit_adder_checker_1_p7), .carry_out(n16_bit_adder_checker_1_p6));
  Clock Clock_2 (.out(n16_bit_adder_checker_1_p4));
  Button Reset_2 (.out(n16_bit_adder_checker_1_p5));
  // _4_Bit_Adder_Checker 4_bit_adder_checker_1: pin names not known; wires that end beside it: n4_bit_adder_checker_1_p1, n4_bit_adder_checker_1_p2, n4_bit_adder_checker_1_p3, n4_bit_adder_checker_1_p4, n4_bit_adder_checker_1_p5, n4_bit_adder_checker_1_p6, n4_bit_adder_checker_1_p7
  _4_Bit_Adder u_4_bit_adder_1 (
    .a(n4_bit_adder_checker_1_p1), .b(n4_bit_adder_checker_1_p2), .carry_in(n4_bit_adder_checker_1_p3),
    .sum(n4_bit_adder_checker_1_p7), .carry_out(n4_bit_adder_checker_1_p6));
  Clock Clock_3 (.out(n4_bit_adder_checker_1_p4));
  Button Reset_3 (.out(n4_bit_adder_checker_1_p5));

  // Notes on the sheet:
  //   To use each checker:
  //   1. Click the Reset button with the poke tool.
  //   2. To step through test cases individually, click the Clock with the poke tool.
  //   The keyboard shortcut for enabling and disabling ticks is Ctrl+K, which you may use instead.
  //   3. To step through test cases automatically, select "Simulate" from the menu, then click "Enable Ticks" to make the clocks cycle between 0 and 1 automatically.
  //   Note: The 16-Bit Adder Checker does not test all possible input combinations.
  //   It will test random values of a and b and display how many your adder handled correctly.
  //   If you have no errors after roughly 2000 test cases, you can expect that your adder is correct.
endmodule

module ALU_Checkers (
);

  wire n4_bit_alu_checker_1_p4, n4_bit_alu_checker_1_p5, n16_bit_alu_checker_1_p4, n16_bit_alu_checker_1_p5;
  wire [2:0] n4_bit_alu_checker_1_p3, n16_bit_alu_checker_1_p3;
  wire [3:0] n4_bit_alu_checker_1_p1, n4_bit_alu_checker_1_p2, n4_bit_alu_checker_1_p6;
  wire [15:0] n16_bit_alu_checker_1_p1, n16_bit_alu_checker_1_p2, n16_bit_alu_checker_1_p6;

  // _4_Bit_ALU_Checker 4_bit_alu_checker_1: pin names not known; wires that end beside it: n4_bit_alu_checker_1_p1, n4_bit_alu_checker_1_p2, n4_bit_alu_checker_1_p3, n4_bit_alu_checker_1_p4, n4_bit_alu_checker_1_p5, n4_bit_alu_checker_1_p6
  _4_Bit_ALU u_4_bit_alu_1 (
    .a(n4_bit_alu_checker_1_p1), .b(n4_bit_alu_checker_1_p2), .operation(n4_bit_alu_checker_1_p3),
    .\output (n4_bit_alu_checker_1_p6));
  Clock Clock (.out(n4_bit_alu_checker_1_p4));
  Button Reset (.out(n4_bit_alu_checker_1_p5));
  // _16_Bit_ALU_Checker 16_bit_alu_checker_1: pin names not known; wires that end beside it: n16_bit_alu_checker_1_p1, n16_bit_alu_checker_1_p2, n16_bit_alu_checker_1_p3, n16_bit_alu_checker_1_p4, n16_bit_alu_checker_1_p5, n16_bit_alu_checker_1_p6
  _16_Bit_ALU u_16_bit_alu_1 (
    .a(n16_bit_alu_checker_1_p1), .b(n16_bit_alu_checker_1_p2), .operation(n16_bit_alu_checker_1_p3),
    .\output (n16_bit_alu_checker_1_p6));
  Clock Clock_2 (.out(n16_bit_alu_checker_1_p4));
  Button Reset_2 (.out(n16_bit_alu_checker_1_p5));

  // Notes on the sheet:
  //   To use each checker:
  //   1. Click the Reset button with the poke tool.
  //   2. To step through test cases individually, click the Clock with the poke tool.
  //   The keyboard shortcut for enabling and disabling ticks is Ctrl+K, which you may use instead.
  //   3. To step through test cases automatically, select "Simulate" from the menu, then click "Enable Ticks" to make the clocks cycle between 0 and 1 automatically.
  //   Note: The 16-Bit ALU Checker does not test all possible input combinations.
  //   It will test random values of a and b for each operation and display how many your ALU handled correctly.
  //   If you have no errors after roughly 500 test cases per operation, you can expect that your ALU is correct.
endmodule

// 000
module _4_bitIsMultipleOf4 (
  input  [3:0] in_1,
  output [3:0] \output 
);

  wire or_1_out;

  or or_1 (or_1_out, in_1[0], in_1[1]);
  not not_1 (\output [0], or_1_out);

  assign \output [3:1] = 3'b000;

  // Notes on the sheet:
  //   We will recieve a 1 bit output, 0 or 1, 1 being true if the first 2 bits are 0 and 0 otherwise.
  //   This tests a 4 bit input to see if it is a multiple of four. The only time this is true is when the first 2 bits are 0. Hence, we use a NOR gate. 
  //   Since we only get 1 output from the NOR gate and we have a 4 bit input, we need a joiner to pad the output with three other 0's b4 transmitting to the MUX
endmodule

module _4_bit_2_sComplementNegation (
  input  [3:0] in_1,
  output [3:0] \output 
);

  wire [3:0] not_1_out;

  assign not_1_out = ~in_1;  // NOT_Gate not_1, 4 bits wide
  _4_Bit_Adder u_4_bit_adder_1 (.a(not_1_out), .b(4'b0000), .carry_in(1'b1), .sum(\output ));  // open: carry_out

  // Notes on the sheet:
  //   Add the 1 like always after flipping the bits. 
  //   Perform 1's complement by negating the input and add the constant 0 to it because Brandonsim will bitch if you put an input.
endmodule

module _4_bit_MultiplyBy5 (
  input  [3:0] in_1,
  output [3:0] \output 
);

  _4_Bit_Adder u_4_bit_adder_1 (.a({in_1[1:0], 2'b00}), .b(in_1), .carry_in(1'b0), .sum(\output ));  // open: carry_out
endmodule

module _16_Bit_Subtraction (
  input  [15:0] in_1,
  input  [15:0] in_2,
  output [15:0] out_3
);

  wire [15:0] not_1_out;

  assign not_1_out = ~in_2;  // NOT_Gate not_1, 16 bits wide
  _16_Bit_Adder u_16_bit_adder_1 (.a(in_1), .b(not_1_out), .carry_in(1'b1), .sum(out_3));  // open: carry_out

  // Notes on the sheet:
  //   output
endmodule

module _16_bit_A_8____1 (
  input  [15:0] in_1,
  output [15:0] \output 
);

  wire not_1_out, or_1_out;

  not not_1 (not_1_out, or_1_out);
  or or_1 (or_1_out, in_1[1], in_1[2]);
  and and_1 (\output [0], in_1[0], not_1_out);

  assign \output [15:1] = {15{1'b0}};

  // Notes on the sheet:
  //   We are testing to see if the remainder is 1
endmodule

module _16_Bit_2_sComplementNegation (
  input  [15:0] in_1,
  output [15:0] \output 
);

  wire [15:0] not_1_out;

  assign not_1_out = ~in_1;  // NOT_Gate not_1, 16 bits wide
  _16_Bit_Adder u_16_bit_adder_1 (.a(not_1_out), .b({16{1'b0}}), .carry_in(1'b1), .sum(\output ));  // open: carry_out
endmodule

module _16_bit_MultiplyBy11 (
  input  [15:0] in_1,
  output [15:0] out_2
);

  wire [15:0] n16_bit_adder_1_sum;

  _16_Bit_Adder u_16_bit_adder_1 (
    .a({in_1[12:0], 3'b000}), .b({in_1[14:0], 1'b0}), .carry_in(1'b0), .sum(n16_bit_adder_1_sum));  // open: carry_out
  _16_Bit_Adder u_16_bit_adder_2 (.a(in_1), .b(n16_bit_adder_1_sum), .carry_in(1'b0), .sum(out_2));  // open: carry_out

  // Notes on the sheet:
  //   Shift the original by three. Shift the original by one.
  //   output
  //   For this, You can do mulitply by 11 by leftshifting the input by 3 and also in a seperate splitter, left shift by 1. Add those two shifted representations and then the sum of that carry should be added to the original representtion. 
endmodule
