// Logisim project hw3.circ as structural Verilog: 7 circuits, main circuit 1-Bit Adder
module _1_Bit_Adder (
  input  a,
  input  b,
  input  carry_in,
  output sum,
  output carry_out
);


  // Notes on the sheet:
  //   Note: Do NOT move any of the pins already in this circuit. Moving the pins may cause the checkers to fail.
endmodule

module _4_Bit_Adder (
  input  [3:0] a,
  input  [3:0] b,
  input  carry_in,
  output [3:0] sum,
  output carry_out
);


  // Notes on the sheet:
  //   Note: Do NOT move any of the pins already in this circuit. Moving the pins may cause the checkers to fail.
endmodule

module _4_Bit_ALU (
  input  [3:0] a,
  input  [3:0] b,
  input  [2:0] operation,
  output [3:0] \output 
);


  // Notes on the sheet:
  //   Note: Do NOT move any of the pins already in this circuit. Moving the pins may cause the checkers to fail.
endmodule

module _16_Bit_Adder (
  input  [15:0] a,
  input  [15:0] b,
  input  carry_in,
  output [15:0] sum,
  output carry_out
);


  // Notes on the sheet:
  //   Note: Do NOT move any of the pins already in this circuit. Moving the pins may cause the checkers to fail.
endmodule

module _16_Bit_ALU (
  input  [15:0] a,
  input  [15:0] b,
  input  [2:0] operation,
  output [15:0] \output 
);


  // Notes on the sheet:
  //   Note: Do NOT move any of the pins already in this circuit. Moving the pins may cause the checkers to fail.
endmodule

module Adder_Checkers (
);

  wire n1_bit_adder_checker_1_p1, n1_bit_adder_checker_1_p2, n1_bit_adder_checker_1_p3,
       n1_bit_adder_checker_1_p4, n1_bit_adder_checker_1_p5, n1_bit_adder_checker_1_p6,
       n1_bit_adder_checker_1_p7, n4_bit_adder_checker_1_p3, n4_bit_adder_checker_1_p4,
       n4_bit_adder_checker_1_p5, n4_bit_adder_checker_1_p6, n16_bit_adder_checker_1_p3,
       n16_bit_adder_checker_1_p4, n16_bit_adder_checker_1_p5, n16_bit_adder_checker_1_p6;
  wire [3:0] n4_bit_adder_checker_1_p1, n4_bit_adder_checker_1_p2, n4_bit_adder_checker_1_p7;
  wire [15:0] n16_bit_adder_checker_1_p1, n16_bit_adder_checker_1_p2, n16_bit_adder_checker_1_p7;

  // _1_Bit_Adder_Checker 1_bit_adder_checker_1: pin names not known; wires that end beside it: n1_bit_adder_checker_1_p1, n1_bit_adder_checker_1_p2, n1_bit_adder_checker_1_p3, n1_bit_adder_checker_1_p4, n1_bit_adder_checker_1_p5, n1_bit_adder_checker_1_p6, n1_bit_adder_checker_1_p7
  Clock Clock (.out(n1_bit_adder_checker_1_p4));
  // _16_Bit_Adder_Checker 16_bit_adder_checker_1: pin names not known; wires that end beside it: n16_bit_adder_checker_1_p1, n16_bit_adder_checker_1_p2, n16_bit_adder_checker_1_p3, n16_bit_adder_checker_1_p4, n16_bit_adder_checker_1_p5, n16_bit_adder_checker_1_p6, n16_bit_adder_checker_1_p7
  _1_Bit_Adder u_1_bit_adder_1 (
    .a(n1_bit_adder_checker_1_p1), .b(n1_bit_adder_checker_1_p2), .carry_in(n1_bit_adder_checker_1_p3),
    .sum(n1_bit_adder_checker_1_p7), .carry_out(n1_bit_adder_checker_1_p6));
  Button Reset (.out(n1_bit_adder_checker_1_p5));
  _16_Bit_Adder u_16_bit_adder_1 (
    .a(n16_bit_adder_checker_1_p1), .b(n16_bit_adder_checker_1_p2), .carry_in(n16_bit_adder_checker_1_p3),
    .sum(n16_bit_adder_checker_1_p7), .carry_out(n16_bit_adder_checker_1_p6));
  Button Reset_2 (.out(n16_bit_adder_checker_1_p5));
  Clock Clock_2 (.out(n16_bit_adder_checker_1_p4));
  // _4_Bit_Adder_Checker 4_bit_adder_checker_1: pin names not known; wires that end beside it: n4_bit_adder_checker_1_p1, n4_bit_adder_checker_1_p2, n4_bit_adder_checker_1_p3, n4_bit_adder_checker_1_p4, n4_bit_adder_checker_1_p5, n4_bit_adder_checker_1_p6, n4_bit_adder_checker_1_p7
  _4_Bit_Adder u_4_bit_adder_1 (
    .a(n4_bit_adder_checker_1_p1), .b(n4_bit_adder_checker_1_p2), .carry_in(n4_bit_adder_checker_1_p3),
    .sum(n4_bit_adder_checker_1_p7), .carry_out(n4_bit_adder_checker_1_p6));
  Button Reset_3 (.out(n4_bit_adder_checker_1_p5));
  Clock Clock_3 (.out(n4_bit_adder_checker_1_p4));

  // Notes on the sheet:
  //   To use each checker:
  //   1. Click the Reset button with the poke tool.
  //   2. To step through test cases individually, click the Clock with the poke tool.
  //   The keyboard shortcut for enabling and disabling ticks is Ctrl+K, which you may use instead.
  //   3. To step through test cases automatically, select "Simulate" from the menu, then click "Enable Ticks" to make the clocks cycle between 0 and 1 automatically.
  //   Note: The 16-Bit Adder Checker does not test all possible input combinations.
  //   It will test random values of a and b and display how many your adder handled correctly.
  //   If you have no errors after roughly 2000 test cases, you can expect that your adder is correct.
endmodule

module ALU_Checkers (
);

  wire n4_bit_alu_checker_1_p4, n4_bit_alu_checker_1_p5, n16_bit_alu_checker_1_p4, n16_bit_alu_checker_1_p5;
  wire [2:0] n4_bit_alu_checker_1_p3, n16_bit_alu_checker_1_p3;
  wire [3:0] n4_bit_alu_checker_1_p1, n4_bit_alu_checker_1_p2, n4_bit_alu_checker_1_p6;
  wire [15:0] n16_bit_alu_checker_1_p1, n16_bit_alu_checker_1_p2, n16_bit_alu_checker_1_p6;

  // _4_Bit_ALU_Checker 4_bit_alu_checker_1: pin names not known; wires that end beside it: n4_bit_alu_checker_1_p1, n4_bit_alu_checker_1_p2, n4_bit_alu_checker_1_p3, n4_bit_alu_checker_1_p4, n4_bit_alu_checker_1_p5, n4_bit_alu_checker_1_p6
  _4_Bit_ALU u_4_bit_alu_1 (
    .a(n4_bit_alu_checker_1_p1), .b(n4_bit_alu_checker_1_p2), .operation(n4_bit_alu_checker_1_p3),
    .\output (n4_bit_alu_checker_1_p6));
  Clock Clock (.out(n4_bit_alu_checker_1_p4));
  Button Reset (.out(n4_bit_alu_checker_1_p5));
  // _16_Bit_ALU_Checker 16_bit_alu_checker_1: pin names not known; wires that end beside it: n16_bit_alu_checker_1_p1, n16_bit_alu_checker_1_p2, n16_bit_alu_checker_1_p3, n16_bit_alu_checker_1_p4, n16_bit_alu_checker_1_p5, n16_bit_alu_checker_1_p6
  _16_Bit_ALU u_16_bit_alu_1 (
    .a(n16_bit_alu_checker_1_p1), .b(n16_bit_alu_checker_1_p2), .operation(n16_bit_alu_checker_1_p3),
    .\output (n16_bit_alu_checker_1_p6));
  Clock Clock_2 (.out(n16_bit_alu_checker_1_p4));
  Button Reset_2 (.out(n16_bit_alu_checker_1_p5));

  // Notes on the sheet:
  //   To use each checker:
  //   1. Click the Reset button with the poke tool.
  //   2. To step through test cases individually, click the Clock with the poke tool.
  //   The keyboard shortcut for enabling and disabling ticks is Ctrl+K, which you may use instead.
  //   3. To step through test cases automatically, select "Simulate" from the menu, then click "Enable Ticks" to make the clocks cycle between 0 and 1 automatically.
  //   Note: The 16-Bit ALU Checker does not test all possible input combinations.
  //   It will test random values of a and b for each operation and display how many your ALU handled correctly.
  //   If you have no errors after roughly 500 test cases per operation, you can expect that your ALU is correct.
endmodule
