// Logisim project hw4.circ as structural Verilog: 4 circuits, main circuit one-hot state machine
module one_hot_state_machine (
  input  CLK,
  input  W,
  input  RST,
  output A,
  output B,
  output C,
  output D
);

  wire _0, _1, _2, _3, _4, _10_out, and_1_out, and_2_out, and_4_out, and_5_out, and_6_out, and_7_out,
       and_8_out, and_9_out, NOR_Output, or_5_out;
  wire [4:0] or_3_out;

  and and_1 (and_1_out, _3, W);
  and and_2 (and_2_out, _2, W);
  and _10 (_10_out, _2, ~W);  // AND_Gate
  or or_1 (or_3_out[3], and_1_out, and_2_out, _10_out);
  and and_3 (or_3_out[1], _0, W);
  and and_4 (and_4_out, _0, ~W);  // AND_Gate
  and and_5 (and_5_out, _3, ~W);  // AND_Gate
  and and_6 (and_6_out, _1, ~W);  // AND_Gate
  and and_7 (and_7_out, _4, ~W);  // AND_Gate
  and and_8 (and_8_out, _1, W);
  and and_9 (and_9_out, _4, W);
  or or_2 (or_3_out[4], and_4_out, and_5_out, and_6_out);
  or or_3 (or_3_out[0], NOR_Output, and_7_out);
  or or_4 (or_3_out[2], and_8_out, and_9_out);
  Register #(.width(5)) register_1 (.D(or_3_out), .Q({_4, _3, _2, _1, _0}), .clk(CLK), .clr(RST));  // open: en
  or or_5 (or_5_out, _0, _1, _2, _3, _4);
  not not_1 (NOR_Output, or_5_out);
  or or_6 (A, _0, _1, _2);
  or or_7 (B, _0, _3, _4);
  or or_8 (C, _1, _3, _4);
  or or_9 (D, _2, _4);

  // Notes on the sheet:
  //   Yamin Mousselli
  //   Do not place anything here!
  //   Implement your state machine here
  //   #8
  //   #9
  //   Moving the input and output pins of this subcircuit will break the tester subcircuit
  //   Going to i = 3
  //   #1
  //   #2
  //   #3
  //   #4
  //   #5
  //   #6
  //   #7
  //   Going to i = 1
  //   Going to i = 4
  //   #5: Going to i = 0
  //   Going to i = 2
  //   The register input is the state your FSM will transition to
  //   The register output is the same as what's in the register. It represent the current state of your FSM
  //   The numbers in the tunnels correspond to where the bit is in the current state before transitioning
  //   The clock is edge triggered and lets the FSM transtion. It ticks at the end of every period, aka clock cycle
  //   OUTPUTS
  //   The NOR gate is for the case when your input is all 0's (00000) and this is another case where you can get to your initiial state. The only way you can get to your initial state is through #5 and when all inputs are all 0 (from the NOR, it will return true if they are).
endmodule

module reduced_state_machine (
  input  CLK,
  input  W,
  input  RST,
  output A,
  output B,
  output C,
  output D
);

  wire _0, _1, _2, and_1_out, and_2_out, and_3_out, and_4_out, and_5_out, and_6_out, and_7_out, and_8_out,
       and_9_out, and_10_out, and_11_out, and_12_out, and_13_out;
  wire [2:0] or_3_out;

  and and_1 (and_1_out, ~_1, ~W, ~_2);  // AND_Gate
  and and_2 (and_2_out, _0, ~W);  // AND_Gate
  and and_3 (and_3_out, W, _2);
  and and_4 (and_4_out, _0, W);
  and and_5 (and_5_out, _1, ~_0);  // AND_Gate
  or or_1 (or_3_out[2], and_1_out, and_2_out);
  or or_2 (or_3_out[1], and_3_out, and_4_out, and_5_out);
  and and_6 (and_6_out, W, ~_0, ~_2);  // AND_Gate
  and and_7 (and_7_out, ~_0, _1);  // AND_Gate
  and and_8 (and_8_out, _1, W);
  Register #(.width(3)) register_1 (.D(or_3_out), .Q({_2, _1, _0}), .clk(CLK), .clr(RST));  // open: en
  or or_3 (or_3_out[0], and_6_out, and_7_out, and_8_out);
  and and_9 (and_9_out, ~_1, ~_0);  // AND_Gate
  and and_10 (and_10_out, _1, _0);
  and and_11 (and_11_out, _1, ~_0);  // AND_Gate
  and and_12 (and_12_out, ~_2, ~_1);  // AND_Gate
  or or_4 (A, and_12_out, and_13_out);
  and and_13 (and_13_out, _1, ~_0);  // AND_Gate
  or or_5 (B, and_9_out, and_10_out);
  or or_6 (C, _2, _0);
  or or_7 (D, _2, and_11_out);

  // Notes on the sheet:
  //   Yamin Mousselli
  //   N2 KMAP
  //   Do not place anything here!
  //   Implement your state machine here
  //   Moving the input and output pins of this subcircuit will break the tester subcircuit
  //   N1 KMAP
  //   N0 KMAP
  //   OUTPUTS
endmodule

module one_hot_checker (
);

  wire NEXT_out, one_hot_checker_1_p2, one_hot_state_machine_1_a, one_hot_state_machine_1_b,
       one_hot_state_machine_1_c, one_hot_state_machine_1_d, RESET_out;

  Clock NEXT (.out(NEXT_out));
  Button RESET (.out(RESET_out));
  // One_Hot_Checker one_hot_checker_1: pin names not known; wires that end beside it: RESET_out, one_hot_checker_1_p2
  one_hot_state_machine one_hot_state_machine_1 (
    .CLK(NEXT_out), .W(one_hot_checker_1_p2), .RST(RESET_out), .A(one_hot_state_machine_1_a),
    .B(one_hot_state_machine_1_b), .C(one_hot_state_machine_1_c), .D(one_hot_state_machine_1_d));
endmodule

module reduced_checker (
);

  wire NEXT_out, reduced_checker_1_p2, reduced_state_machine_1_a, reduced_state_machine_1_b,
       reduced_state_machine_1_c, reduced_state_machine_1_d, RESET_out;

  Clock NEXT (.out(NEXT_out));
  Button RESET (.out(RESET_out));
  // Reduced_Checker reduced_checker_1: pin names not known; wires that end beside it: RESET_out, reduced_checker_1_p2
  reduced_state_machine reduced_state_machine_1 (
    .CLK(NEXT_out), .W(reduced_checker_1_p2), .RST(RESET_out), .A(reduced_state_machine_1_a),
    .B(reduced_state_machine_1_b), .C(reduced_state_machine_1_c), .D(reduced_state_machine_1_d));
endmodule
