// Logisim project timed_lab_1.circ as structural Verilog: 3 circuits, main circuit state machine
module state_machine (
  input  CLK,
  input  G,
  input  RST,
  output W,
  output X,
  output Y,
  output Z
);

  wire _0, _1, _2, _3, _4, _4____5, _5____5, and_1_out, and_2_out, and_3_out, and_4_out, and_5_out,
       and_6_out, and_7_out, and_8_out, NOR_Output, or_5_out, Out5;
  wire [4:0] or_3_out;

  and and_1 (and_1_out, _0, ~G);  // AND_Gate
  and and_2 (and_2_out, _1, G);
  and and_3 (and_3_out, _4, G);
  or or_1 (Out5, _4____5, _5____5);
  and and_4 (and_4_out, _3, G);
  and and_5 (and_5_out, _3, ~G);  // AND_Gate
  and and_6 (and_6_out, _2, G);
  or or_2 (or_3_out[2], and_1_out, and_2_out, and_3_out);
  or or_3 (or_3_out[0], NOR_Output, and_4_out, and_5_out, and_6_out);
  and and_7 (and_7_out, _4, ~G);  // AND_Gate
  and and_8 (and_8_out, _2, ~G);  // AND_Gate
  or or_4 (or_3_out[3], and_7_out, and_8_out);
  and and_9 (or_3_out[1], _0, G);
  and and_10 (or_3_out[4], _1, ~G);  // AND_Gate
  Register #(.width(5)) register_1 (.D(or_3_out), .Q({_4, _3, _2, _1, _0}), .clk(CLK), .clr(RST));  // open: en
  or or_5 (or_5_out, _0, _1, _2, _3, _4);
  or or_6 (W, _0, _1, _2, _3);
  or or_7 (X, _1, _4);
  not not_1 (NOR_Output, or_5_out);
  or or_8 (Y, _1, _4);
  or or_9 (Z, _2, _3);

  // Notes on the sheet:
  //   Going to State 2
  //   Going To State 0
  //   Do not place anything here!
  //   Implement your state machine here
  //   Going to State 4
  //   Moving the input and output pins of this subcircuit will break the tester subcircuit
  //   Going to State 1
  //   Going To State 3
  //   OUTPUTS
endmodule

module one_hot_checker (
);

  wire NEXT_out, one_hot_checker_1_p2, RESET_out, state_machine_1_w, state_machine_1_x, state_machine_1_y,
       state_machine_1_z;

  Clock NEXT (.out(NEXT_out));
  Button RESET (.out(RESET_out));
  // One_Hot_Checker one_hot_checker_1: pin names not known; wires that end beside it: RESET_out, one_hot_checker_1_p2
  state_machine state_machine_1 (
    .CLK(NEXT_out), .G(one_hot_checker_1_p2), .RST(RESET_out), .W(state_machine_1_w), .X(state_machine_1_x),
    .Y(state_machine_1_y), .Z(state_machine_1_z));
endmodule

module reduced_checker (
);

  wire NEXT_out, reduced_checker_1_p2, RESET_out, state_machine_1_w, state_machine_1_x, state_machine_1_y,
       state_machine_1_z;

  Clock NEXT (.out(NEXT_out));
  Button RESET (.out(RESET_out));
  // Reduced_Checker reduced_checker_1: pin names not known; wires that end beside it: RESET_out, reduced_checker_1_p2
  state_machine state_machine_1 (
    .CLK(NEXT_out), .G(reduced_checker_1_p2), .RST(RESET_out), .W(state_machine_1_w), .X(state_machine_1_x),
    .Y(state_machine_1_y), .Z(state_machine_1_z));
endmodule
